# Fritzing sketch OpenerPcr (saved by Fritzing 0.8.5b)
circuit board: 8cm x 6.8cm
breadboards: 7

parts:
  Peltier = Peltier Element
  External_power_supply = Power plug [part_number="Power supply"]
  External_power_supply_connector1 = female pin header, 4 pins [form="♀ (female)"]
  JT = female pin header, 2 pins [form="♀ (female)"]
  T = Temperature Sensor (Thermistor) [thermistor_type=NTC package=THT]
  R_T = Resistor [tolerance=±5% resistance=10k package=THT]
  J_RLY = female pin header, 5 pins [form="♀ (female)"]
  LCD = LCD screen
  J_LCD = male pin header, 16 pins [form="♂ (male)"]
  J_POT = female pin header, 3 pins [form="♀ (female)"]
  R_IL1 = Resistor [tolerance=±5% resistance=1k package=THT]
  R_IL2 = Resistor [tolerance=±5% resistance=1k package=THT]
  LED_IL1_H = LED - 5mm [color="Red (633nm)" package="5 mm [THT]"]
  LED_IL1_C = LED - 5mm [color="Blue (430nm)" package="5 mm [THT]"]
  LED_IL2_C = LED - 5mm [color="Blue (430nm)" package="5 mm [THT]"]
  LED_IL2_H = LED - 5mm [color="Red (633nm)" package="5 mm [THT]"]
  JHCLEDs = female pin header, 8 pins [form="♀ (female)"]
  ROT_LCD = Rotary Potentiometer (Small) [maximum_resistance=100kΩ package=THT]
  Onderdeel1 = Arduino Uno (Rev3)

nets:
  N1: Peltier.pin1, External_power_supply_connector1.pin3
  N2: Peltier.pin2, External_power_supply_connector1.pin4
  N3: External_power_supply.GND, External_power_supply_connector1.pin2
  N4: External_power_supply.VCC, External_power_supply_connector1.pin1
  VDD: JT.pin1, T.pin_0, J_RLY.pin1, LCD.VDD, J_LCD.pin15, J_POT.pin1, LED_IL1_C.cathode, LED_IL2_C.cathode, JHCLEDs.pin3, JHCLEDs.pin7, ROT_LCD.leg1, Onderdeel1.5V
  N5: JT.pin2, T.pin_1, R_T.Pin_0, Onderdeel1.A0
  VSS: R_T.Pin_1, J_RLY.pin5, LCD.VSS, LCD.R/W, J_LCD.pin12, J_LCD.pin16, J_POT.pin3, LED_IL1_H.cathode, LED_IL2_H.cathode, JHCLEDs.pin2, JHCLEDs.pin6, ROT_LCD.leg2, Onderdeel1.GND
  N6: J_RLY.pin2, R_IL1.Pin_1, Onderdeel1.D2
  N7: J_RLY.pin3, R_IL2.Pin_1, Onderdeel1.D3_PWM
  N8: J_RLY.pin4, Onderdeel1.D5_PWM
  N9: LCD.V0, J_LCD.pin14, J_POT.pin2, ROT_LCD.wiper
  N10: LCD.RS, J_LCD.pin13, Onderdeel1.D8
  N11: LCD.E, J_LCD.pin11, Onderdeel1.D9_PWM
  N12: LCD.DB0, J_LCD.pin10
  N13: LCD.DB1, J_LCD.pin9
  N14: LCD.DB2, J_LCD.pin8
  N15: LCD.DB3, J_LCD.pin7
  N16: LCD.DB4, J_LCD.pin6, Onderdeel1.D10_PWM/SS
  N17: LCD.DB5, J_LCD.pin5, Onderdeel1.D11_PWM/MOSI
  N18: LCD.DB6, J_LCD.pin4, Onderdeel1.D12/MISO
  N19: LCD.DB7, J_LCD.pin3, Onderdeel1.D13/SCK
  N20: LCD.LED+, J_LCD.pin2
  N21: LCD.LED-, J_LCD.pin1
  N22: R_IL1.Pin_0, LED_IL1_H.anode, LED_IL1_C.anode, JHCLEDs.pin1, JHCLEDs.pin4
  N23: R_IL2.Pin_0, LED_IL2_C.anode, LED_IL2_H.anode, JHCLEDs.pin5, JHCLEDs.pin8

notes:
  H bridge breakout board
  External power
  Thermistor board
  1: Termistor pin #1
  2: Termistor pin #2
  Our external power supply
  1: external power source A
  2: external power source B
  3: load pin A
  4: load pin B
  Power and ground
  1. 5 V, for powering the relay board
  2. 1: IL1, Peltier heats if HIGH
  3. 2: IL2, Peltier heats if HIGH
  4. PWM fan control
  5. GND
  Relay board
  OpenerPCR v.1.6
  DIY Bio Groningen
  Version 1.6.1:
  - Let components be found on non-Fablab computer
  Version 1.6:
  - Added LEDs that show cooling/heating
  Version 1.5:
  - Connect fan to PWM
  Version 1.4:
  - added one pin for fan on/off
  - removed H-bridge breakout board connector from PCB
  Version 1.3:
  - fixed error (again) in thermistor connection
  - removed thermistor from PCB: use the connectors for it
  Version 1.2:
  - fixed error in thermistor connection
  Version 1.1:
  - use an extra pin, to be able to turn the Peltier off
  - removed some unused connectors
  2014-04-06
  1: Heating, +
  2: Heating, -
  3: Cooling, +
  4: Cooling, -
  5: Heating, +
  6: Heating, -
  7: Cooling, +
  8: Cooling, -
  LCD display will be upside-down in this view; the screen will go towards the closest outside of the PCB
  Heating and cooling indication LEDS
  Relay board is seperate from the board
  Thermistor
